// Logisim project Processador.circ as structural Verilog
module Processador (
  input  in_1,
  input  in_2,
  input  in_3,
  input  in_4,
  input  in_5,
  input  in_6,
  input  in_7
);

  wire amux_1_a0, amux_1_a1, amux_1_a2, amux_1_a3, amux_1_a4, amux_1_a5, banco_mir_1_q0, banco_mir_1_q1,
       banco_mir_1_q2, banco_mir_1_q3, banco_mir_1_q4, banco_mir_1_q5, banco_mir_1_q6, banco_mir_1_q7,
       banco_mir_1_q8, banco_mir_1_q9, banco_mir_1_q10, banco_mir_1_q11, banco_mir_1_q12, banco_mir_1_q13,
       banco_mir_1_q14, banco_mir_1_q15, banco_mir_1_q16, banco_mir_1_q17, banco_mir_1_q18,
       banco_registrador_1_a0, banco_registrador_1_a1, banco_registrador_1_a2, banco_registrador_1_a3,
       banco_registrador_1_a4, banco_registrador_1_a5, banco_registrador_1_b0, banco_registrador_1_b1,
       banco_registrador_1_b2, banco_registrador_1_b3, banco_registrador_1_b4, banco_registrador_1_b5,
       clock_1_out, clock_2_out, clock_3_out, clock_4_out, clock_5_out, incrementador_1_s0,
       incrementador_1_s1, incrementador_1_s2, incrementador_1_s3, incrementador_1_s4, latch_a_1_s0,
       latch_a_1_s1, latch_a_1_s2, latch_a_1_s3, latch_a_1_s4, latch_a_1_s5, latch_b_1_s0, latch_b_1_s1,
       latch_b_1_s2, latch_b_1_s3, latch_b_1_s4, latch_b_1_s5, mar_1_s0, mbr_1_am0, mbr_1_am1, mbr_1_am2,
       mbr_1_am3, mbr_1_am4, mbr_1_am5, mbr_1_sext0, mbr_1_sext1, mbr_1_sext2, mbr_1_sext3, mbr_1_sext4,
       mbr_1_sext5, mir_1_q0, mir_1_q1, mir_1_q2, mir_1_q3, mir_1_q4, mir_1_q5, mir_1_q6, mir_1_q7, mir_1_q8,
       mir_1_q9, mir_1_q10, mir_1_q11, mir_1_q12, mir_1_q13, mir_1_q14, mir_1_q15, mir_1_q16, mir_1_q17,
       mir_1_q18, programa_1_s0, programa_1_s1, programa_1_s2, programa_1_s3, programa_1_s4,
       shifter_projeto_1_s0, shifter_projeto_1_s1, shifter_projeto_1_s2, shifter_projeto_1_s3,
       shifter_projeto_1_s4, shifter_projeto_1_s5, transcriver_1_sext0, transcriver_1_sext1,
       transcriver_1_sext2, transcriver_1_sext3, transcriver_1_sext4, transcriver_1_sext5, ula_6bits_1_r0,
       ula_6bits_1_r1, ula_6bits_1_r2, ula_6bits_1_r3, ula_6bits_1_r4, ula_6bits_1_r5;
  wire [1:0] transcriver_1_dis4;
  wire [3:0] transcriver_1_dis0;

  Hex_Digit_Display #(.decimalPoint("false")) hex_digit_display_1 (.value({2'b00, transcriver_1_dis4}));
  Hex_Digit_Display #(.decimalPoint("false")) hex_digit_display_2 (.value(transcriver_1_dis0));
  TRANSCRIVER transcriver_1 (
    .T_R(mar_1_s0), .TEC2(in_4), .TEC3(in_5), .TEC4(in_6), .TEC5(in_7), .BUSEXT0(mbr_1_sext0),
    .BUSEXT1(mbr_1_sext1), .BUSEXT2(mbr_1_sext2), .BUSEXT3(mbr_1_sext3), .BUSEXT4(mbr_1_sext4),
    .BUSEXT5(mbr_1_sext5), .TEC0(in_2), .TEC1(in_3), .SEXT5(transcriver_1_sext5),
    .DIS0(transcriver_1_dis0[0]), .DIS1(transcriver_1_dis0[1]), .DIS2(transcriver_1_dis0[2]),
    .DIS3(transcriver_1_dis0[3]), .DIS4(transcriver_1_dis4[0]), .DIS5(transcriver_1_dis4[1]),
    .SEXT0(transcriver_1_sext0), .SEXT1(transcriver_1_sext1), .SEXT2(transcriver_1_sext2),
    .SEXT3(transcriver_1_sext3), .SEXT4(transcriver_1_sext4));
  MAR mar_1 (
    .B5(latch_b_1_s5), .B4(latch_b_1_s4), .B3(latch_b_1_s3), .B2(latch_b_1_s2), .B1(latch_b_1_s1),
    .B0(latch_b_1_s0), .CLOCK(clock_2_out), .ENABLE(mir_1_q13), .S0(mar_1_s0));  // open: RESET, S5, S4, S3, S2, S1
  MBR mbr_1 (
    .in_1(mir_1_q11), .in_2(mir_1_q10), .CLOCK(clock_1_out), .ENABLE(mir_1_q12), .EEXT0(transcriver_1_sext5),
    .EEXT1(transcriver_1_sext4), .EEXT2(transcriver_1_sext3), .EEXT3(transcriver_1_sext2),
    .EEXT4(transcriver_1_sext1), .EEXT5(transcriver_1_sext0), .BC0(shifter_projeto_1_s0),
    .BC1(shifter_projeto_1_s1), .BC2(shifter_projeto_1_s2), .BC3(shifter_projeto_1_s3),
    .BC4(shifter_projeto_1_s4), .BC5(shifter_projeto_1_s5), .SEXT0(mbr_1_sext0), .SEXT1(mbr_1_sext1),
    .SEXT2(mbr_1_sext2), .SEXT3(mbr_1_sext3), .SEXT4(mbr_1_sext4), .SEXT5(mbr_1_sext5), .AM0(mbr_1_am0),
    .AM1(mbr_1_am1), .AM2(mbr_1_am2), .AM3(mbr_1_am3), .AM4(mbr_1_am4), .AM5(mbr_1_am5));
  Clock #(.lowDuration(3)) clock_1 (.out(clock_1_out));
  Clock #(.lowDuration(3), .phaseOffset(1)) clock_2 (.out(clock_2_out));
  Clock #(.lowDuration(3), .phaseOffset(2)) clock_3 (.out(clock_3_out));
  Clock #(.lowDuration(3), .phaseOffset(3)) clock_4 (.out(clock_4_out));
  Banco_Registrador banco_registrador_1 (
    .AA2(mir_1_q5), .AA1(mir_1_q4), .AA0(mir_1_q3), .BB2(mir_1_q2), .BB1(mir_1_q1), .BB0(mir_1_q0),
    .E5(shifter_projeto_1_s5), .E4(shifter_projeto_1_s4), .E3(shifter_projeto_1_s3),
    .E2(shifter_projeto_1_s2), .E1(shifter_projeto_1_s1), .E0(shifter_projeto_1_s0), .C2(mir_1_q8),
    .C1(mir_1_q7), .C0(mir_1_q6), .in_10(clock_1_out), .ENABLE(mir_1_q9), .A5(banco_registrador_1_a5),
    .A4(banco_registrador_1_a4), .A3(banco_registrador_1_a3), .A2(banco_registrador_1_a2),
    .A1(banco_registrador_1_a1), .A0(banco_registrador_1_a0), .B5(banco_registrador_1_b5),
    .B4(banco_registrador_1_b4), .B3(banco_registrador_1_b3), .B2(banco_registrador_1_b2),
    .B1(banco_registrador_1_b1), .B0(banco_registrador_1_b0));
  Amux amux_1 (
    .M5(latch_a_1_s5), .M4(latch_a_1_s4), .M3(latch_a_1_s3), .M2(latch_a_1_s2), .M1(latch_a_1_s1),
    .M0(latch_a_1_s0), .L5(mbr_1_am5), .L4(mbr_1_am4), .L3(mbr_1_am3), .L2(mbr_1_am2), .L1(mbr_1_am1),
    .L0(mbr_1_am0), .E0(mir_1_q18), .A5(amux_1_a5), .A4(amux_1_a4), .A3(amux_1_a3), .A2(amux_1_a2),
    .A1(amux_1_a1), .A0(amux_1_a0));
  Shifter_projeto shifter_projeto_1 (
    .R5(ula_6bits_1_r5), .R4(ula_6bits_1_r4), .R3(ula_6bits_1_r3), .R2(ula_6bits_1_r2), .R1(ula_6bits_1_r1),
    .R0(ula_6bits_1_r0), .Ee1(mir_1_q15), .Ee0(mir_1_q14), .S5(shifter_projeto_1_s5),
    .S4(shifter_projeto_1_s4), .S3(shifter_projeto_1_s3), .S2(shifter_projeto_1_s2),
    .S1(shifter_projeto_1_s1), .S0(shifter_projeto_1_s0));
  LATCH_A latch_a_1 (
    .A5(banco_registrador_1_a5), .A4(banco_registrador_1_a4), .A3(banco_registrador_1_a3),
    .A2(banco_registrador_1_a2), .A1(banco_registrador_1_a1), .A0(banco_registrador_1_a0),
    .ENABLE(clock_3_out), .S5(latch_a_1_s5), .S4(latch_a_1_s4), .S3(latch_a_1_s3), .S2(latch_a_1_s2),
    .S1(latch_a_1_s1), .S0(latch_a_1_s0));
  ULA_6bits ula_6bits_1 (
    .A4(amux_1_a4), .A3(amux_1_a3), .A2(amux_1_a2), .A1(amux_1_a1), .A0(amux_1_a0), .E1(mir_1_q17),
    .E0(mir_1_q16), .B5(latch_b_1_s5), .B4(latch_b_1_s4), .B3(latch_b_1_s3), .B2(latch_b_1_s2),
    .B1(latch_b_1_s1), .B0(latch_b_1_s0), .A5(amux_1_a5), .R5(ula_6bits_1_r5), .R4(ula_6bits_1_r4),
    .R3(ula_6bits_1_r3), .R2(ula_6bits_1_r2), .R1(ula_6bits_1_r1), .R0(ula_6bits_1_r0));
  Clock Tempo_do_Clock ();  // open: out
  LATCH_B latch_b_1 (
    .B5(banco_registrador_1_b5), .B4(banco_registrador_1_b4), .B3(banco_registrador_1_b3),
    .B2(banco_registrador_1_b2), .B1(banco_registrador_1_b1), .B0(banco_registrador_1_b0),
    .ENABLE(clock_3_out), .S5(latch_b_1_s5), .S4(latch_b_1_s4), .S3(latch_b_1_s3), .S2(latch_b_1_s2),
    .S1(latch_b_1_s1), .S0(latch_b_1_s0));
  Clock #(.lowDuration(3), .phaseOffset(3)) clock_5 (.out(clock_5_out));
  Incrementador incrementador_1 (
    .DADOS(clock_5_out), .CLEAR(in_1), .S0(incrementador_1_s0), .S1(incrementador_1_s1),
    .S2(incrementador_1_s2), .S3(incrementador_1_s3), .S4(incrementador_1_s4));
  Programa programa_1 (
    .E0(incrementador_1_s0), .E1(incrementador_1_s1), .E2(incrementador_1_s2), .E3(incrementador_1_s3),
    .E4(incrementador_1_s4), .S0(programa_1_s0), .S1(programa_1_s1), .S2(programa_1_s2), .S3(programa_1_s3),
    .S4(programa_1_s4));
  Banco_Mir banco_mir_1 (
    .in_1(programa_1_s4), .in_2(programa_1_s3), .in_3(programa_1_s2), .in_4(programa_1_s1),
    .in_5(programa_1_s0), .Q0(banco_mir_1_q0), .Q1(banco_mir_1_q1), .Q2(banco_mir_1_q2), .Q3(banco_mir_1_q3),
    .Q4(banco_mir_1_q4), .Q5(banco_mir_1_q5), .Q6(banco_mir_1_q6), .Q7(banco_mir_1_q7), .Q8(banco_mir_1_q8),
    .Q9(banco_mir_1_q9), .Q10(banco_mir_1_q10), .Q11(banco_mir_1_q11), .Q12(banco_mir_1_q12),
    .Q13(banco_mir_1_q13), .Q14(banco_mir_1_q14), .Q15(banco_mir_1_q15), .Q16(banco_mir_1_q16),
    .Q17(banco_mir_1_q17), .Q18(banco_mir_1_q18));  // open: Q19, Q20, Q21, Q22, Q23
  MIR mir_1 (
    .CLOCK(clock_4_out), .DECC2(banco_mir_1_q6), .DECA(banco_mir_1_q5), .DECA1(banco_mir_1_q4),
    .DECA2(banco_mir_1_q3), .DECB(banco_mir_1_q2), .DECB1(banco_mir_1_q1), .DECB2(banco_mir_1_q0),
    .AMUX(banco_mir_1_q18), .ULA(banco_mir_1_q17), .ULA1(banco_mir_1_q16), .SH(banco_mir_1_q15),
    .SH1(banco_mir_1_q14), .MAR(banco_mir_1_q13), .MBR(banco_mir_1_q12), .RD(banco_mir_1_q11),
    .WR(banco_mir_1_q10), .ENC(banco_mir_1_q9), .DECC(banco_mir_1_q8), .DECC1(banco_mir_1_q7), .Q6(mir_1_q6),
    .Q5(mir_1_q5), .Q4(mir_1_q4), .Q3(mir_1_q3), .Q2(mir_1_q2), .Q1(mir_1_q1), .Q0(mir_1_q0),
    .Q18(mir_1_q18), .Q17(mir_1_q17), .Q16(mir_1_q16), .Q15(mir_1_q15), .Q14(mir_1_q14), .Q13(mir_1_q13),
    .Q12(mir_1_q12), .Q11(mir_1_q11), .Q10(mir_1_q10), .Q9(mir_1_q9), .Q8(mir_1_q8), .Q7(mir_1_q7));

  // Notes on the sheet:
  //   MBR/RESGISTRADOR
  //   MAR
  //   LATCH
  //   MIR
  //   00 Add R0,R1
  //   01 Not R0
  //   02 Nand R0,R1
  //   03 Sub R0,R1
  //   04 Shl R0, 1
  //   05 Shr R0, 1
  //   06 Mov R0, R1
  //   07 Mov R0, R2
  //   08 Mov R0, R3
  //   09 Mov R0, R4
  //   10 Mov R0, R5
  //   11 Mov R0, R6
  //   12 Mov R0, R7
  //   13 Mov R1, R0
  //   14 Mov R2, R0
  //   15 Mov R3, R0
  //   16 Mov R4, R0
  //   17 Mov R5, R0
  //   18 Mov R6, R0
  //   19 Mov R7, R0
  //   20 Mov Mar, R0
  //   21 Mov R0, Mbr
  //   22 Mov Mbr, R0
  //   23 In
  //   24 Out
  //   00000
  //   00001
  //   00010
  //   00011
  //   00100
  //   00101
  //   00110
  //   00111
  //   01000
  //   01001
  //   01010
  //   01011
  //   01100
  //   01101
  //   01110
  //   10001
  //   10010
  //   10011
  //   01111
  //   10000
  //   10100
  //   10101
  //   10110
  //   10111
  //   11000
endmodule

module Somador_1bit (
  input  A,
  input  B,
  input  Cin,
  output SUM,
  output Cout
);

  wire and_1_out, and_2_out, xor_1_out;

  xor xor_1 (xor_1_out, A, B);
  and and_1 (and_1_out, A, B);
  xor xor_2 (SUM, xor_1_out, Cin);
  and and_2 (and_2_out, xor_1_out, Cin);
  xor xor_3 (Cout, and_2_out, and_1_out);
endmodule

module Somador_6bit (
  input  A5,
  input  A4,
  input  A3,
  input  A2,
  input  A1,
  input  A0,
  input  B5,
  input  B4,
  input  B3,
  input  B2,
  input  B1,
  input  B0,
  output Cout,
  output SUM5,
  output SUM4,
  output SUM3,
  output SUM2,
  output SUM1,
  output SUM0
);

  wire somador_1bit_1_cout, somador_1bit_2_cout, somador_1bit_3_cout, somador_1bit_4_cout,
       somador_1bit_5_cout;

  Somador_1bit somador_1bit_1 (.A(A0), .B(B0), .SUM(SUM0), .Cout(somador_1bit_1_cout));  // open: Cin
  Somador_1bit somador_1bit_2 (.A(A1), .B(B1), .Cin(somador_1bit_1_cout), .SUM(SUM1), .Cout(somador_1bit_2_cout));
  Somador_1bit somador_1bit_3 (.A(A2), .B(B2), .Cin(somador_1bit_2_cout), .SUM(SUM2), .Cout(somador_1bit_3_cout));
  Somador_1bit somador_1bit_4 (.A(A3), .B(B3), .Cin(somador_1bit_3_cout), .SUM(SUM3), .Cout(somador_1bit_4_cout));
  Somador_1bit somador_1bit_5 (.A(A4), .B(B4), .Cin(somador_1bit_4_cout), .SUM(SUM4), .Cout(somador_1bit_5_cout));
  Somador_1bit somador_1bit_6 (.A(A5), .B(B5), .Cin(somador_1bit_5_cout), .SUM(SUM5), .Cout(Cout));
endmodule

module Subtrator_1bit (
  input  A,
  input  B,
  input  Bin,
  output DIF,
  output Bout
);

  wire and_1_out, and_2_out, not_1_out, not_2_out, xor_1_out;

  not not_1 (not_1_out, A);
  xor xor_1 (xor_1_out, A, B);
  and and_1 (and_1_out, not_1_out, B);
  not not_2 (not_2_out, xor_1_out);
  xor xor_2 (DIF, Bin, xor_1_out);
  and and_2 (and_2_out, not_2_out, Bin);
  or or_1 (Bout, and_2_out, and_1_out);
endmodule

module Subtrator_6bits (
  input  A5,
  input  A4,
  input  A3,
  input  A2,
  input  A1,
  input  A0,
  input  B5,
  input  B4,
  input  B3,
  input  B2,
  input  B1,
  input  B0,
  output Bout,
  output DIF5,
  output DIF4,
  output DIF3,
  output DIF2,
  output DIF1,
  output DIF0
);

  wire subtrator_1bit_1_bout, subtrator_1bit_2_bout, subtrator_1bit_3_bout, subtrator_1bit_4_bout,
       subtrator_1bit_5_bout;

  Subtrator_1bit subtrator_1bit_1 (.A(A0), .B(B0), .DIF(DIF0), .Bout(subtrator_1bit_1_bout));  // open: Bin
  Subtrator_1bit subtrator_1bit_2 (
    .A(A1), .B(B1), .Bin(subtrator_1bit_1_bout), .DIF(DIF1), .Bout(subtrator_1bit_2_bout));
  Subtrator_1bit subtrator_1bit_3 (
    .A(A2), .B(B2), .Bin(subtrator_1bit_2_bout), .DIF(DIF2), .Bout(subtrator_1bit_3_bout));
  Subtrator_1bit subtrator_1bit_4 (
    .A(A3), .B(B3), .Bin(subtrator_1bit_3_bout), .DIF(DIF3), .Bout(subtrator_1bit_4_bout));
  Subtrator_1bit subtrator_1bit_5 (
    .A(A4), .B(B4), .Bin(subtrator_1bit_4_bout), .DIF(DIF4), .Bout(subtrator_1bit_5_bout));
  Subtrator_1bit subtrator_1bit_6 (.A(A5), .B(B5), .Bin(subtrator_1bit_5_bout), .DIF(DIF5), .Bout(Bout));
endmodule

module Buffer_6bits (
  input  A5,
  input  A4,
  input  A3,
  input  A2,
  input  A1,
  input  A0,
  output BUF5,
  output BUF4,
  output BUF3,
  output BUF2,
  output BUF1,
  output BUF0
);

  buf buffer_1 (BUF0, A0);
  buf buffer_2 (BUF1, A1);
  buf buffer_3 (BUF2, A2);
  buf buffer_4 (BUF3, A3);
  buf buffer_5 (BUF4, A4);
  buf buffer_6 (BUF5, A5);
endmodule

module Nand_6bits (
  input  A5,
  input  A4,
  input  A3,
  input  A2,
  input  A1,
  input  A0,
  input  B5,
  input  B4,
  input  B3,
  input  B2,
  input  B1,
  input  B0,
  output NAND5,
  output NAND4,
  output NAND3,
  output NAND2,
  output NAND1,
  output NAND0
);

  nand nand_1 (NAND0, A0, B0);
  nand nand_2 (NAND1, A1, B1);
  nand nand_3 (NAND2, A2, B2);
  nand nand_4 (NAND3, A3, B3);
  nand nand_5 (NAND4, A4, B4);
  nand nand_6 (NAND5, A5, B5);
endmodule

module Multiplexador_2x1 (
  input  E0,
  input  S1,
  input  S0,
  output Y
);

  wire and_1_out, and_2_out, decode_1x2_1_s0, decode_1x2_1_s1;

  Decode_1x2 decode_1x2_1 (.E0(E0), .S1(decode_1x2_1_s1), .S0(decode_1x2_1_s0));
  and and_1 (and_1_out, S0, decode_1x2_1_s0);
  and and_2 (and_2_out, decode_1x2_1_s1, S1);
  or or_1 (Y, and_1_out, and_2_out);
endmodule

module Multiplexador_4x1 (
  input  E1,
  input  E0,
  input  S3,
  input  S2,
  input  S1,
  input  S0,
  output Y
);

  wire and_1_out, and_2_out, and_3_out, and_4_out, decode_2bits_1_s0, decode_2bits_1_s1, decode_2bits_1_s2,
       decode_2bits_1_s3;

  Decode_2bits decode_2bits_1 (
    .E1(E1), .E0(E0), .S3(decode_2bits_1_s3), .S2(decode_2bits_1_s2), .S1(decode_2bits_1_s1),
    .S0(decode_2bits_1_s0));
  and and_1 (and_1_out, decode_2bits_1_s0, S0);
  and and_2 (and_2_out, decode_2bits_1_s1, S1);
  and and_3 (and_3_out, decode_2bits_1_s2, S2);
  and and_4 (and_4_out, decode_2bits_1_s3, S3);
  or or_1 (Y, and_1_out, and_2_out, and_3_out, and_4_out);
endmodule

module MULTIPLEXADOR_8X1 (
  input  E2,
  input  E1,
  input  E0,
  input  M7,
  input  M6,
  input  M5,
  input  M4,
  input  M3,
  input  M2,
  input  M1,
  input  M0,
  output Y
);

  wire and_1_out, and_2_out, and_3_out, and_4_out, and_5_out, and_6_out, and_7_out, and_8_out,
       decode_3x8_1_s0, decode_3x8_1_s1, decode_3x8_1_s2, decode_3x8_1_s3, decode_3x8_1_s4, decode_3x8_1_s5,
       decode_3x8_1_s6, decode_3x8_1_s7;

  DECODE_3X8 decode_3x8_1 (
    .E2(E2), .E1(E1), .E0(E0), .S7(decode_3x8_1_s7), .S6(decode_3x8_1_s6), .S5(decode_3x8_1_s5),
    .S4(decode_3x8_1_s4), .S3(decode_3x8_1_s3), .S2(decode_3x8_1_s2), .S1(decode_3x8_1_s1),
    .S0(decode_3x8_1_s0));
  and and_1 (and_1_out, M0, decode_3x8_1_s0);
  and and_2 (and_2_out, M1, decode_3x8_1_s1);
  and and_3 (and_3_out, M2, decode_3x8_1_s2);
  and and_4 (and_4_out, M3, decode_3x8_1_s3);
  and and_5 (and_5_out, M4, decode_3x8_1_s4);
  and and_6 (and_6_out, M5, decode_3x8_1_s5);
  and and_7 (and_7_out, M6, decode_3x8_1_s6);
  and and_8 (and_8_out, M7, decode_3x8_1_s7);
  or or_1 (Y, and_1_out, and_2_out, and_3_out, and_4_out, and_5_out, and_6_out, and_7_out, and_8_out);
endmodule

module Amux (
  input  E0,
  input  M5,
  input  M4,
  input  M3,
  input  M2,
  input  M1,
  input  M0,
  input  L5,
  input  L4,
  input  L3,
  input  L2,
  input  L1,
  input  L0,
  output A5,
  output A4,
  output A3,
  output A2,
  output A1,
  output A0
);

  Multiplexador_2x1 multiplexador_2x1_1 (.S1(L0), .S0(M0), .E0(E0), .Y(A0));
  Multiplexador_2x1 multiplexador_2x1_2 (.S1(L1), .S0(M1), .E0(E0), .Y(A1));
  Multiplexador_2x1 multiplexador_2x1_3 (.S1(L2), .S0(M2), .E0(E0), .Y(A2));
  Multiplexador_2x1 multiplexador_2x1_4 (.S1(L3), .S0(M3), .E0(E0), .Y(A3));
  Multiplexador_2x1 multiplexador_2x1_5 (.S1(L4), .S0(M4), .E0(E0), .Y(A4));
  Multiplexador_2x1 multiplexador_2x1_6 (.S1(L5), .S0(M5), .E0(E0), .Y(A5));

  // Notes on the sheet:
  //   MBR
  //   LATCH A
endmodule

module Decode_1x2 (
  input  E0,
  output S1,
  output S0
);

  not not_1 (S0, E0);

  assign S1 = E0;
endmodule

module Decode_2bits (
  input  E1,
  input  E0,
  output S3,
  output S2,
  output S1,
  output S0
);

  wire not_1_out, not_2_out;

  not not_1 (not_1_out, E1);
  not not_2 (not_2_out, E0);
  and and_1 (S0, not_2_out, not_1_out);
  and and_2 (S1, not_1_out, E0);
  and and_3 (S2, not_2_out, E1);
  and and_4 (S3, E0, E1);
endmodule

module DECODE_3X8 (
  input  E2,
  input  E1,
  input  E0,
  output S7,
  output S6,
  output S5,
  output S4,
  output S3,
  output S2,
  output S1,
  output S0
);

  wire not_1_out, not_2_out, not_3_out;

  not not_1 (not_1_out, E2);
  not not_2 (not_2_out, E1);
  not not_3 (not_3_out, E0);
  and and_1 (S0, not_3_out, not_2_out, not_1_out);
  and and_2 (S1, E0, not_2_out, not_1_out);
  and and_3 (S2, E1, not_3_out, not_1_out);
  and and_4 (S3, E0, E1, not_1_out);
  and and_5 (S4, not_3_out, not_2_out, E2);
  and and_6 (S5, E0, not_2_out, E2);
  and and_7 (S6, not_3_out, E1, E2);
  and and_8 (S7, E0, E1, E2);
endmodule

module DECODE_4X16 (
  input  E3,
  input  E2,
  input  E1,
  input  E0,
  output Y15,
  output Y14,
  output Y13,
  output Y12,
  output Y11,
  output Y20,
  output Y9,
  output Y8,
  output Y7,
  output Y6,
  output Y5,
  output Y4,
  output Y3,
  output Y2,
  output Y1,
  output Y0
);

  wire not_1_out, not_2_out, not_3_out, not_4_out;

  not not_1 (not_1_out, E3);
  not not_2 (not_2_out, E2);
  not not_3 (not_3_out, E1);
  not not_4 (not_4_out, E0);
  and and_1 (Y0, not_4_out, not_3_out, not_2_out, not_1_out);
  and and_2 (Y1, E0, not_3_out, not_2_out, not_1_out);
  and and_3 (Y2, not_4_out, E1, not_2_out, not_1_out);
  and and_4 (Y3, E0, E1, not_2_out, not_1_out);
  and and_5 (Y4, not_4_out, not_3_out, E2, not_1_out);
  and and_6 (Y5, E0, not_3_out, E2, not_1_out);
  and and_7 (Y6, not_4_out, E1, E2, not_1_out);
  and and_8 (Y7, E0, E1, E2, not_1_out);
  and and_9 (Y8, not_4_out, not_3_out, not_2_out, E3);
  and and_10 (Y9, E0, not_3_out, not_2_out, E3);
  and and_11 (Y20, not_4_out, E1, not_2_out, E3);
  and and_12 (Y11, E0, E1, not_2_out, E3);
  and and_13 (Y12, not_4_out, not_3_out, E2, E3);
  and and_14 (Y13, E0, not_3_out, E2, E3);
  and and_15 (Y14, not_4_out, E1, E2, E3);
  and and_16 (Y15, E0, E1, E2, E3);
endmodule

module Resgitrador (
  input  E1,
  input  E0,
  input  CLOCK,
  input  C5,
  input  C4,
  input  C3,
  input  C2,
  input  C1,
  input  C0,
  output A5,
  output A4,
  output A3,
  output A2,
  output A1,
  output A0,
  output B5,
  output B4,
  output B3,
  output B2,
  output B1,
  output B0
);

  wire [1:0] d_ff_5_q;
  wire [3:0] d_ff_1_q;

  D_Flip_Flop d_ff_1 (.D(C0), .clk(CLOCK), .Q(d_ff_1_q[0]));  // open: Qn, preset, reset
  D_Flip_Flop d_ff_2 (.D(C1), .clk(CLOCK), .Q(d_ff_1_q[1]));  // open: Qn, preset, reset
  D_Flip_Flop d_ff_3 (.D(C2), .clk(CLOCK), .Q(d_ff_1_q[2]));  // open: Qn, preset, reset
  D_Flip_Flop d_ff_4 (.D(C3), .clk(CLOCK), .Q(d_ff_1_q[3]));  // open: Qn, preset, reset
  D_Flip_Flop d_ff_5 (.D(C4), .clk(CLOCK), .Q(d_ff_5_q[0]));  // open: Qn, preset, reset
  D_Flip_Flop d_ff_6 (.D(C5), .clk(CLOCK), .Q(d_ff_5_q[1]));  // open: Qn, preset, reset
  assign B0 = E0 ? d_ff_1_q[0] : 1'bz;  // Controlled_Buffer controlled_buffer_1
  assign A0 = E1 ? d_ff_1_q[0] : 1'bz;  // Controlled_Buffer controlled_buffer_2
  assign B1 = E0 ? d_ff_1_q[1] : 1'bz;  // Controlled_Buffer controlled_buffer_3
  assign A1 = E1 ? d_ff_1_q[1] : 1'bz;  // Controlled_Buffer controlled_buffer_4
  assign B2 = E0 ? d_ff_1_q[2] : 1'bz;  // Controlled_Buffer controlled_buffer_5
  assign A2 = E1 ? d_ff_1_q[2] : 1'bz;  // Controlled_Buffer controlled_buffer_6
  assign B3 = E0 ? d_ff_1_q[3] : 1'bz;  // Controlled_Buffer controlled_buffer_7
  assign A3 = E1 ? d_ff_1_q[3] : 1'bz;  // Controlled_Buffer controlled_buffer_8
  assign B4 = E0 ? d_ff_5_q[0] : 1'bz;  // Controlled_Buffer controlled_buffer_9
  assign A4 = E1 ? d_ff_5_q[0] : 1'bz;  // Controlled_Buffer controlled_buffer_10
  assign B5 = E0 ? d_ff_5_q[1] : 1'bz;  // Controlled_Buffer controlled_buffer_11
  assign A5 = E1 ? d_ff_5_q[1] : 1'bz;  // Controlled_Buffer controlled_buffer_12
  Hex_Digit_Display #(.decimalPoint("false")) hex_digit_display_1 (.value({2'b00, d_ff_5_q}));
  Hex_Digit_Display #(.decimalPoint("false")) hex_digit_display_2 (.value(d_ff_1_q));
endmodule

module FLIP_FLOP_D (
  input  D,
  input  E,
  output out_3
);

  wire latch_1_q;

  latch latch_1 (.D(D), .E(E), .Q(latch_1_q));  // open: Q_0
  latch latch_2 (.D(latch_1_q), .E(E), .Q(out_3));  // open: Q_0
endmodule

module LATCH_A (
  input  ENABLE,
  input  A5,
  input  A4,
  input  A3,
  input  A2,
  input  A1,
  input  A0,
  output S5,
  output S4,
  output S3,
  output S2,
  output S1,
  output S0
);

  D_Flip_Flop d_ff_1 (.D(A0), .clk(ENABLE), .Q(S0));  // open: Qn, preset, reset
  D_Flip_Flop d_ff_2 (.D(A1), .clk(ENABLE), .Q(S1));  // open: Qn, preset, reset
  D_Flip_Flop d_ff_3 (.D(A2), .clk(ENABLE), .Q(S2));  // open: Qn, preset, reset
  D_Flip_Flop d_ff_4 (.D(A3), .clk(ENABLE), .Q(S3));  // open: Qn, preset, reset
  D_Flip_Flop d_ff_5 (.D(A4), .clk(ENABLE), .Q(S4));  // open: Qn, preset, reset
  D_Flip_Flop d_ff_6 (.D(A5), .clk(ENABLE), .Q(S5));  // open: Qn, preset, reset
endmodule

module LATCH_B (
  input  ENABLE,
  input  B5,
  input  B4,
  input  B3,
  input  B2,
  input  B1,
  input  B0,
  output S5,
  output S4,
  output S3,
  output S2,
  output S1,
  output S0
);

  D_Flip_Flop d_ff_1 (.D(B0), .clk(ENABLE), .Q(S0));  // open: Qn, preset, reset
  D_Flip_Flop d_ff_2 (.D(B1), .clk(ENABLE), .Q(S1));  // open: Qn, preset, reset
  D_Flip_Flop d_ff_3 (.D(B2), .clk(ENABLE), .Q(S2));  // open: Qn, preset, reset
  D_Flip_Flop d_ff_4 (.D(B3), .clk(ENABLE), .Q(S3));  // open: Qn, preset, reset
  D_Flip_Flop d_ff_5 (.D(B4), .clk(ENABLE), .Q(S4));  // open: Qn, preset, reset
  D_Flip_Flop d_ff_6 (.D(B5), .clk(ENABLE), .Q(S5));  // open: Qn, preset, reset
endmodule

module latch (
  input  D,
  input  E,
  output Q,
  output Q_0
);

  wire nand_1_out, nand_2_out, nand_3_out;

  nand nand_1 (nand_1_out, D, D);
  nand nand_2 (nand_2_out, D, E);
  nand nand_3 (nand_3_out, E, nand_1_out);
  nand nand_4 (Q, nand_2_out, Q_0);
  nand nand_5 (Q_0, nand_3_out, Q);
endmodule

module MAR (
  input  CLOCK,
  input  ENABLE,
  input  RESET,
  input  B5,
  input  B4,
  input  B3,
  input  B2,
  input  B1,
  input  B0,
  output S5,
  output S4,
  output S3,
  output S2,
  output S1,
  output S0
);

  wire and_1_out, and_2_out, and_3_out, and_4_out, and_5_out, and_6_out;

  and and_1 (and_1_out, ENABLE, CLOCK);
  and and_2 (and_2_out, ENABLE, CLOCK);
  and and_3 (and_3_out, ENABLE, CLOCK);
  and and_4 (and_4_out, ENABLE, CLOCK);
  and and_5 (and_5_out, ENABLE, CLOCK);
  and and_6 (and_6_out, ENABLE, CLOCK);
  D_Flip_Flop D0 (.D(B0), .clk(and_1_out), .Q(S0), .reset(RESET));  // open: Qn, preset
  D_Flip_Flop D1 (.D(B1), .clk(and_2_out), .Q(S1), .reset(RESET));  // open: Qn, preset
  D_Flip_Flop D2 (.D(B2), .clk(and_3_out), .Q(S2), .reset(RESET));  // open: Qn, preset
  D_Flip_Flop D3 (.D(B3), .clk(and_4_out), .Q(S3), .reset(RESET));  // open: Qn, preset
  D_Flip_Flop D4 (.D(B4), .clk(and_5_out), .Q(S4), .reset(RESET));  // open: Qn, preset
  D_Flip_Flop D5 (.D(B5), .clk(and_6_out), .Q(S5), .reset(RESET));  // open: Qn, preset
endmodule

module MBR (
  input  in_1,
  input  in_2,
  input  CLOCK,
  input  ENABLE,
  input  EEXT0,
  input  EEXT1,
  input  EEXT2,
  input  EEXT3,
  input  EEXT4,
  input  EEXT5,
  input  BC0,
  input  BC1,
  input  BC2,
  input  BC3,
  input  BC4,
  input  BC5,
  output SEXT0,
  output SEXT1,
  output SEXT2,
  output SEXT3,
  output SEXT4,
  output SEXT5,
  output AM0,
  output AM1,
  output AM2,
  output AM3,
  output AM4,
  output AM5
);

  wire and_1_out, controlled_buffer_1_out, controlled_buffer_5_out, controlled_buffer_9_out,
       controlled_buffer_13_out, controlled_buffer_17_out, controlled_buffer_21_out, d_ff_1_q, d_ff_1_qn,
       d_ff_2_q, d_ff_2_qn, d_ff_3_q, d_ff_3_qn, d_ff_4_q, d_ff_4_qn, d_ff_5_q, d_ff_5_qn, d_ff_6_q,
       d_ff_6_qn, decode_2bits_1_s0, decode_2bits_1_s1, decode_2bits_1_s2, decode_2bits_1_s3, or_1_out,
       or_2_out, or_3_out, or_4_out, or_5_out, or_6_out, or_7_out, or_8_out, or_9_out, or_10_out, or_11_out,
       or_12_out;

  Decode_2bits decode_2bits_1 (
    .E1(in_2), .E0(in_1), .S3(decode_2bits_1_s3), .S2(decode_2bits_1_s2), .S1(decode_2bits_1_s1),
    .S0(decode_2bits_1_s0));
  // NoConnect on decode_2bits_1_s3
  and and_1 (and_1_out, CLOCK, ENABLE);
  or or_1 (or_1_out, decode_2bits_1_s0, decode_2bits_1_s1);
  assign controlled_buffer_1_out = or_1_out ? BC0 : 1'bz;  // Controlled_Buffer controlled_buffer_1
  D_Flip_Flop d_ff_1 (
    .D(controlled_buffer_1_out), .clk(and_1_out), .Q(d_ff_1_q), .Qn(d_ff_1_qn));  // open: preset, reset
  assign controlled_buffer_1_out = decode_2bits_1_s2 ? EEXT0 : 1'bz;  // Controlled_Buffer controlled_buffer_2
  assign AM0 = or_2_out ? d_ff_1_q : 1'bz;  // Controlled_Buffer controlled_buffer_3
  // NoConnect on d_ff_1_qn
  or or_2 (or_2_out, decode_2bits_1_s2, decode_2bits_1_s0);
  assign SEXT0 = decode_2bits_1_s1 ? d_ff_1_q : 1'bz;  // Controlled_Buffer controlled_buffer_4
  or or_3 (or_3_out, decode_2bits_1_s0, decode_2bits_1_s1);
  assign controlled_buffer_5_out = or_3_out ? BC1 : 1'bz;  // Controlled_Buffer controlled_buffer_5
  assign controlled_buffer_5_out = decode_2bits_1_s2 ? EEXT1 : 1'bz;  // Controlled_Buffer controlled_buffer_6
  D_Flip_Flop d_ff_2 (
    .D(controlled_buffer_5_out), .clk(and_1_out), .Q(d_ff_2_q), .Qn(d_ff_2_qn));  // open: preset, reset
  or or_4 (or_4_out, decode_2bits_1_s2, decode_2bits_1_s0);
  assign AM1 = or_4_out ? d_ff_2_q : 1'bz;  // Controlled_Buffer controlled_buffer_7
  // NoConnect on d_ff_2_qn
  assign SEXT1 = decode_2bits_1_s1 ? d_ff_2_q : 1'bz;  // Controlled_Buffer controlled_buffer_8
  assign controlled_buffer_9_out = or_5_out ? BC2 : 1'bz;  // Controlled_Buffer controlled_buffer_9
  or or_5 (or_5_out, decode_2bits_1_s0, decode_2bits_1_s1);
  assign controlled_buffer_9_out = decode_2bits_1_s2 ? EEXT2 : 1'bz;  // Controlled_Buffer controlled_buffer_10
  D_Flip_Flop d_ff_3 (
    .D(controlled_buffer_9_out), .clk(and_1_out), .Q(d_ff_3_q), .Qn(d_ff_3_qn));  // open: preset, reset
  // NoConnect on d_ff_3_qn
  or or_6 (or_6_out, decode_2bits_1_s2, decode_2bits_1_s0);
  assign AM2 = or_6_out ? d_ff_3_q : 1'bz;  // Controlled_Buffer controlled_buffer_11
  assign SEXT2 = decode_2bits_1_s1 ? d_ff_3_q : 1'bz;  // Controlled_Buffer controlled_buffer_12
  or or_7 (or_7_out, decode_2bits_1_s0, decode_2bits_1_s1);
  assign controlled_buffer_13_out = or_7_out ? BC3 : 1'bz;  // Controlled_Buffer controlled_buffer_13
  D_Flip_Flop d_ff_4 (
    .D(controlled_buffer_13_out), .clk(and_1_out), .Q(d_ff_4_q), .Qn(d_ff_4_qn));  // open: preset, reset
  assign controlled_buffer_13_out = decode_2bits_1_s2 ? EEXT3 : 1'bz;  // Controlled_Buffer controlled_buffer_14
  assign AM3 = or_8_out ? d_ff_4_q : 1'bz;  // Controlled_Buffer controlled_buffer_15
  // NoConnect on d_ff_4_qn
  or or_8 (or_8_out, decode_2bits_1_s2, decode_2bits_1_s0);
  assign SEXT3 = decode_2bits_1_s1 ? d_ff_4_q : 1'bz;  // Controlled_Buffer controlled_buffer_16
  or or_9 (or_9_out, decode_2bits_1_s0, decode_2bits_1_s1);
  assign controlled_buffer_17_out = or_9_out ? BC4 : 1'bz;  // Controlled_Buffer controlled_buffer_17
  assign controlled_buffer_17_out = decode_2bits_1_s2 ? EEXT4 : 1'bz;  // Controlled_Buffer controlled_buffer_18
  D_Flip_Flop d_ff_5 (
    .D(controlled_buffer_17_out), .clk(and_1_out), .Q(d_ff_5_q), .Qn(d_ff_5_qn));  // open: preset, reset
  or or_10 (or_10_out, decode_2bits_1_s2, decode_2bits_1_s0);
  assign AM4 = or_10_out ? d_ff_5_q : 1'bz;  // Controlled_Buffer controlled_buffer_19
  // NoConnect on d_ff_5_qn
  assign SEXT4 = decode_2bits_1_s1 ? d_ff_5_q : 1'bz;  // Controlled_Buffer controlled_buffer_20
  or or_11 (or_11_out, decode_2bits_1_s0, decode_2bits_1_s1);
  assign controlled_buffer_21_out = or_11_out ? BC5 : 1'bz;  // Controlled_Buffer controlled_buffer_21
  assign controlled_buffer_21_out = decode_2bits_1_s2 ? EEXT5 : 1'bz;  // Controlled_Buffer controlled_buffer_22
  assign AM5 = or_12_out ? d_ff_6_q : 1'bz;  // Controlled_Buffer controlled_buffer_23
  D_Flip_Flop d_ff_6 (
    .D(controlled_buffer_21_out), .clk(and_1_out), .Q(d_ff_6_q), .Qn(d_ff_6_qn));  // open: preset, reset
  // NoConnect on d_ff_6_qn
  or or_12 (or_12_out, decode_2bits_1_s2, decode_2bits_1_s0);
  assign SEXT5 = decode_2bits_1_s1 ? d_ff_6_q : 1'bz;  // Controlled_Buffer controlled_buffer_24
endmodule

module Banco_Registrador (
  input  AA2,
  input  AA1,
  input  AA0,
  input  BB2,
  input  BB1,
  input  BB0,
  input  C2,
  input  C1,
  input  C0,
  input  in_10,
  input  ENABLE,
  input  E5,
  input  E4,
  input  E3,
  input  E2,
  input  E1,
  input  E0,
  output A5,
  output A4,
  output A3,
  output A2,
  output A1,
  output A0,
  output B5,
  output B4,
  output B3,
  output B2,
  output B1,
  output B0
);

  wire and_1_out, and_2_out, and_3_out, and_4_out, and_5_out, and_6_out, and_7_out, and_8_out, and_9_out,
       decode_3x8_1_s0, decode_3x8_1_s1, decode_3x8_1_s2, decode_3x8_1_s3, decode_3x8_1_s4, decode_3x8_1_s5,
       decode_3x8_1_s6, decode_3x8_1_s7, decode_3x8_2_s0, decode_3x8_2_s1, decode_3x8_2_s2, decode_3x8_2_s3,
       decode_3x8_2_s4, decode_3x8_2_s5, decode_3x8_2_s6, decode_3x8_2_s7, decode_3x8_3_s0, decode_3x8_3_s1,
       decode_3x8_3_s2, decode_3x8_3_s3, decode_3x8_3_s4, decode_3x8_3_s5, decode_3x8_3_s6, decode_3x8_3_s7;

  DECODE_3X8 decode_3x8_1 (
    .E2(C2), .E1(C1), .E0(C0), .S7(decode_3x8_1_s7), .S6(decode_3x8_1_s6), .S5(decode_3x8_1_s5),
    .S4(decode_3x8_1_s4), .S3(decode_3x8_1_s3), .S2(decode_3x8_1_s2), .S1(decode_3x8_1_s1),
    .S0(decode_3x8_1_s0));
  and and_1 (and_1_out, in_10, ENABLE);
  and and_2 (and_2_out, decode_3x8_1_s0, and_1_out);
  and and_3 (and_3_out, decode_3x8_1_s1, and_1_out);
  and and_4 (and_4_out, decode_3x8_1_s2, and_1_out);
  and and_5 (and_5_out, decode_3x8_1_s3, and_1_out);
  and and_6 (and_6_out, decode_3x8_1_s4, and_1_out);
  and and_7 (and_7_out, decode_3x8_1_s5, and_1_out);
  and and_8 (and_8_out, decode_3x8_1_s6, and_1_out);
  and and_9 (and_9_out, decode_3x8_1_s7, and_1_out);
  Resgitrador R0 (
    .C5(E5), .C4(E4), .C3(E3), .C2(E2), .C1(E1), .C0(E0), .CLOCK(and_2_out), .E1(decode_3x8_2_s0),
    .E0(decode_3x8_3_s0), .A5(A5), .A4(A4), .A3(A3), .A2(A2), .A1(A1), .A0(A0), .B5(B5), .B4(B4), .B3(B3),
    .B2(B2), .B1(B1), .B0(B0));
  Resgitrador R1 (
    .C5(E5), .C4(E4), .C3(E3), .C2(E2), .C1(E1), .C0(E0), .CLOCK(and_3_out), .E1(decode_3x8_2_s1),
    .E0(decode_3x8_3_s1), .A5(A5), .A4(A4), .A3(A3), .A2(A2), .A1(A1), .A0(A0), .B5(B5), .B4(B4), .B3(B3),
    .B2(B2), .B1(B1), .B0(B0));
  Resgitrador R2 (
    .C5(E5), .C4(E4), .C3(E3), .C2(E2), .C1(E1), .C0(E0), .CLOCK(and_4_out), .E1(decode_3x8_2_s2),
    .E0(decode_3x8_3_s2), .A5(A5), .A4(A4), .A3(A3), .A2(A2), .A1(A1), .A0(A0), .B5(B5), .B4(B4), .B3(B3),
    .B2(B2), .B1(B1), .B0(B0));
  Resgitrador R3 (
    .C5(E5), .C4(E4), .C3(E3), .C2(E2), .C1(E1), .C0(E0), .CLOCK(and_5_out), .E1(decode_3x8_2_s3),
    .E0(decode_3x8_3_s3), .A5(A5), .A4(A4), .A3(A3), .A2(A2), .A1(A1), .A0(A0), .B5(B5), .B4(B4), .B3(B3),
    .B2(B2), .B1(B1), .B0(B0));
  Resgitrador R4 (
    .C5(E5), .C4(E4), .C3(E3), .C2(E2), .C1(E1), .C0(E0), .CLOCK(and_6_out), .E1(decode_3x8_2_s4),
    .E0(decode_3x8_3_s4), .A5(A5), .A4(A4), .A3(A3), .A2(A2), .A1(A1), .A0(A0), .B5(B5), .B4(B4), .B3(B3),
    .B2(B2), .B1(B1), .B0(B0));
  Resgitrador R5 (
    .C5(E5), .C4(E4), .C3(E3), .C2(E2), .C1(E1), .C0(E0), .CLOCK(and_7_out), .E1(decode_3x8_2_s5),
    .E0(decode_3x8_3_s5), .A5(A5), .A4(A4), .A3(A3), .A2(A2), .A1(A1), .A0(A0), .B5(B5), .B4(B4), .B3(B3),
    .B2(B2), .B1(B1), .B0(B0));
  Resgitrador R6 (
    .C5(E5), .C4(E4), .C3(E3), .C2(E2), .C1(E1), .C0(E0), .CLOCK(and_8_out), .E1(decode_3x8_2_s6),
    .E0(decode_3x8_3_s6), .A5(A5), .A4(A4), .A3(A3), .A2(A2), .A1(A1), .A0(A0), .B5(B5), .B4(B4), .B3(B3),
    .B2(B2), .B1(B1), .B0(B0));
  Resgitrador R7 (
    .C5(E5), .C4(E4), .C3(E3), .C2(E2), .C1(E1), .C0(E0), .CLOCK(and_9_out), .E1(decode_3x8_2_s7),
    .E0(decode_3x8_3_s7), .A5(A5), .A4(A4), .A3(A3), .A2(A2), .A1(A1), .A0(A0), .B5(B5), .B4(B4), .B3(B3),
    .B2(B2), .B1(B1), .B0(B0));
  DECODE_3X8 decode_3x8_2 (
    .E2(AA2), .E1(AA1), .E0(AA0), .S7(decode_3x8_2_s7), .S6(decode_3x8_2_s6), .S5(decode_3x8_2_s5),
    .S4(decode_3x8_2_s4), .S3(decode_3x8_2_s3), .S2(decode_3x8_2_s2), .S1(decode_3x8_2_s1),
    .S0(decode_3x8_2_s0));
  DECODE_3X8 decode_3x8_3 (
    .E2(BB2), .E1(BB1), .E0(BB0), .S7(decode_3x8_3_s7), .S6(decode_3x8_3_s6), .S5(decode_3x8_3_s5),
    .S4(decode_3x8_3_s4), .S3(decode_3x8_3_s3), .S2(decode_3x8_3_s2), .S1(decode_3x8_3_s1),
    .S0(decode_3x8_3_s0));
  Clock Tempo_do_Clock ();  // open: out
endmodule

module ROM_PROJETO (
  input  E3,
  input  E2,
  input  E1,
  input  E0,
  output Y5,
  output Y4,
  output Y3,
  output Y2,
  output Y1,
  output Y0
);

  wire decode_4x16_1_y0, decode_4x16_1_y1, decode_4x16_1_y2, decode_4x16_1_y3, decode_4x16_1_y4,
       decode_4x16_1_y5, decode_4x16_1_y6, decode_4x16_1_y7, decode_4x16_1_y8, decode_4x16_1_y9,
       decode_4x16_1_y11, decode_4x16_1_y12, decode_4x16_1_y13, decode_4x16_1_y14, decode_4x16_1_y15,
       decode_4x16_1_y20;

  DECODE_4X16 decode_4x16_1 (
    .E3(E3), .E2(E2), .E1(E1), .E0(E0), .Y5(decode_4x16_1_y5), .Y4(decode_4x16_1_y4), .Y3(decode_4x16_1_y3),
    .Y2(decode_4x16_1_y2), .Y1(decode_4x16_1_y1), .Y0(decode_4x16_1_y0), .Y15(decode_4x16_1_y15),
    .Y14(decode_4x16_1_y14), .Y13(decode_4x16_1_y13), .Y12(decode_4x16_1_y12), .Y11(decode_4x16_1_y11),
    .Y20(decode_4x16_1_y20), .Y9(decode_4x16_1_y9), .Y8(decode_4x16_1_y8), .Y7(decode_4x16_1_y7),
    .Y6(decode_4x16_1_y6));
  // OR_Gate or_1 is placed but not wired
  // OR_Gate or_2 is placed but not wired
  // OR_Gate or_3 is placed but not wired
  // OR_Gate or_4 is placed but not wired
  // OR_Gate or_5 is placed but not wired
  // OR_Gate or_6 is placed but not wired
  // OR_Gate or_7 is placed but not wired
endmodule

module ULA_6bits (
  input  A5,
  input  A4,
  input  A3,
  input  A2,
  input  A1,
  input  A0,
  input  B5,
  input  B4,
  input  B3,
  input  B2,
  input  B1,
  input  B0,
  input  E1,
  input  E0,
  output R5,
  output R4,
  output R3,
  output R2,
  output R1,
  output R0
);

  wire buffer_6bits_1_buf0, buffer_6bits_1_buf1, buffer_6bits_1_buf2, buffer_6bits_1_buf3,
       buffer_6bits_1_buf4, buffer_6bits_1_buf5, nand_6bits_1_nand0, nand_6bits_1_nand1, nand_6bits_1_nand2,
       nand_6bits_1_nand3, nand_6bits_1_nand4, nand_6bits_1_nand5, somador_6bit_1_cout, somador_6bit_1_sum0,
       somador_6bit_1_sum1, somador_6bit_1_sum2, somador_6bit_1_sum3, somador_6bit_1_sum4,
       somador_6bit_1_sum5, subtrator_6bits_1_bout, subtrator_6bits_1_dif0, subtrator_6bits_1_dif1,
       subtrator_6bits_1_dif2, subtrator_6bits_1_dif3, subtrator_6bits_1_dif4, subtrator_6bits_1_dif5;

  Somador_6bit somador_6bit_1 (
    .A5(A5), .A4(A4), .A3(A3), .A2(A2), .A1(A1), .A0(A0), .B5(B5), .B4(B4), .B3(B3), .B2(B2), .B1(B1),
    .B0(B0), .Cout(somador_6bit_1_cout), .SUM5(somador_6bit_1_sum5), .SUM4(somador_6bit_1_sum4),
    .SUM3(somador_6bit_1_sum3), .SUM2(somador_6bit_1_sum2), .SUM1(somador_6bit_1_sum1),
    .SUM0(somador_6bit_1_sum0));
  Buffer_6bits buffer_6bits_1 (
    .A5(A5), .A4(A4), .A3(A3), .A2(A2), .A1(A1), .A0(A0), .BUF5(buffer_6bits_1_buf5),
    .BUF4(buffer_6bits_1_buf4), .BUF3(buffer_6bits_1_buf3), .BUF2(buffer_6bits_1_buf2),
    .BUF1(buffer_6bits_1_buf1), .BUF0(buffer_6bits_1_buf0));
  Nand_6bits nand_6bits_1 (
    .A5(A5), .A4(A4), .A3(A3), .A2(A2), .A1(A1), .A0(A0), .B5(B5), .B4(B4), .B3(B3), .B2(B2), .B1(B1),
    .B0(B0), .NAND5(nand_6bits_1_nand5), .NAND4(nand_6bits_1_nand4), .NAND3(nand_6bits_1_nand3),
    .NAND2(nand_6bits_1_nand2), .NAND1(nand_6bits_1_nand1), .NAND0(nand_6bits_1_nand0));
  Subtrator_6bits subtrator_6bits_1 (
    .A5(A5), .A4(A4), .A3(A3), .A2(A2), .A1(A1), .A0(A0), .B5(B5), .B4(B4), .B3(B3), .B2(B2), .B1(B1),
    .B0(B0), .Bout(subtrator_6bits_1_bout), .DIF5(subtrator_6bits_1_dif5), .DIF4(subtrator_6bits_1_dif4),
    .DIF3(subtrator_6bits_1_dif3), .DIF2(subtrator_6bits_1_dif2), .DIF1(subtrator_6bits_1_dif1),
    .DIF0(subtrator_6bits_1_dif0));
  LED led_1 (.in(somador_6bit_1_cout));
  LED led_2 (.in(somador_6bit_1_sum5));
  LED led_3 (.in(somador_6bit_1_sum4));
  LED led_4 (.in(somador_6bit_1_sum3));
  LED led_5 (.in(somador_6bit_1_sum2));
  LED led_6 (.in(somador_6bit_1_sum1));
  LED led_7 (.in(somador_6bit_1_sum0));
  LED led_8 (.in(buffer_6bits_1_buf5));
  LED led_9 (.in(buffer_6bits_1_buf4));
  LED led_10 (.in(buffer_6bits_1_buf3));
  LED led_11 (.in(buffer_6bits_1_buf2));
  LED led_12 (.in(buffer_6bits_1_buf1));
  LED led_13 (.in(buffer_6bits_1_buf0));
  LED led_14 (.in(nand_6bits_1_nand5));
  LED led_15 (.in(nand_6bits_1_nand4));
  LED led_16 (.in(nand_6bits_1_nand3));
  LED led_17 (.in(nand_6bits_1_nand2));
  LED led_18 (.in(nand_6bits_1_nand1));
  LED led_19 (.in(nand_6bits_1_nand0));
  LED led_20 (.in(subtrator_6bits_1_bout));
  LED led_21 (.in(subtrator_6bits_1_dif5));
  LED led_22 (.in(subtrator_6bits_1_dif4));
  LED led_23 (.in(subtrator_6bits_1_dif3));
  LED led_24 (.in(subtrator_6bits_1_dif2));
  LED led_25 (.in(subtrator_6bits_1_dif1));
  LED led_26 (.in(subtrator_6bits_1_dif0));
  Multiplexador_4x1 multiplexador_4x1_1 (
    .S3(subtrator_6bits_1_dif0), .S2(nand_6bits_1_nand0), .S1(buffer_6bits_1_buf0), .S0(somador_6bit_1_sum0),
    .E1(E1), .E0(E0), .Y(R0));
  Multiplexador_4x1 multiplexador_4x1_2 (
    .S3(subtrator_6bits_1_dif1), .S2(nand_6bits_1_nand1), .S1(buffer_6bits_1_buf1), .S0(somador_6bit_1_sum1),
    .E1(E1), .E0(E0), .Y(R1));
  Multiplexador_4x1 multiplexador_4x1_3 (
    .S3(subtrator_6bits_1_dif2), .S2(nand_6bits_1_nand2), .S1(buffer_6bits_1_buf2), .S0(somador_6bit_1_sum2),
    .E1(E1), .E0(E0), .Y(R2));
  Multiplexador_4x1 multiplexador_4x1_4 (
    .S3(subtrator_6bits_1_dif3), .S2(nand_6bits_1_nand3), .S1(buffer_6bits_1_buf3), .S0(somador_6bit_1_sum3),
    .E1(E1), .E0(E0), .Y(R3));
  Multiplexador_4x1 multiplexador_4x1_5 (
    .S3(subtrator_6bits_1_dif4), .S2(nand_6bits_1_nand4), .S1(buffer_6bits_1_buf4), .S0(somador_6bit_1_sum4),
    .E1(E1), .E0(E0), .Y(R4));
  Multiplexador_4x1 multiplexador_4x1_6 (
    .S3(subtrator_6bits_1_bout), .S2(nand_6bits_1_nand5), .S1(buffer_6bits_1_buf5), .S0(somador_6bit_1_sum5),
    .E1(E1), .E0(E0), .Y(R5));

  // Notes on the sheet:
  //   SOMADOR
  //   BUFFER
  //   NAND
  //   sUBTRATOR
  //   CONTROLADOR
endmodule

module Shifter_projeto (
  input  Ee1,
  input  Ee0,
  input  R5,
  input  R4,
  input  R3,
  input  R2,
  input  R1,
  input  R0,
  output S5,
  output S4,
  output S3,
  output S2,
  output S1,
  output S0
);

  Multiplexador_4x1 multiplexador_4x1_1 (.S3(1'b0), .S2(1'b0), .S1(R4), .S0(R5), .E1(Ee1), .E0(Ee0), .Y(S5));
  Multiplexador_4x1 multiplexador_4x1_2 (.S3(1'b0), .S2(R5), .S1(R3), .S0(R4), .E1(Ee1), .E0(Ee0), .Y(S4));
  Multiplexador_4x1 multiplexador_4x1_3 (.S3(1'b0), .S2(R4), .S1(R2), .S0(R3), .E1(Ee1), .E0(Ee0), .Y(S3));
  Multiplexador_4x1 multiplexador_4x1_4 (.S3(1'b0), .S2(R3), .S1(R1), .S0(R2), .E1(Ee1), .E0(Ee0), .Y(S2));
  Multiplexador_4x1 multiplexador_4x1_5 (.S3(1'b0), .S2(R2), .S1(R0), .S0(R1), .E1(Ee1), .E0(Ee0), .Y(S1));
  Multiplexador_4x1 multiplexador_4x1_6 (.S3(1'b0), .S2(R1), .S1(1'b0), .S0(R0), .E1(Ee1), .E0(Ee0), .Y(S0));

  // Notes on the sheet:
  //   00 = Não deslocar
  //   11 = Não utilizado
  //   01 = LSL (1 Bit para a esquerda)
  //   10 = LSR = (1 Bit para a direita)
endmodule

module MIR (
  input  CLOCK,
  input  AMUX,
  input  ULA,
  input  ULA1,
  input  SH,
  input  SH1,
  input  MAR,
  input  MBR,
  input  RD,
  input  WR,
  input  ENC,
  input  DECC,
  input  DECC1,
  input  DECC2,
  input  DECA,
  input  DECA1,
  input  DECA2,
  input  DECB,
  input  DECB1,
  input  DECB2,
  output Q18,
  output Q17,
  output Q16,
  output Q15,
  output Q14,
  output Q13,
  output Q12,
  output Q11,
  output Q10,
  output Q9,
  output Q8,
  output Q7,
  output Q6,
  output Q5,
  output Q4,
  output Q3,
  output Q2,
  output Q1,
  output Q0
);

  D_Flip_Flop d_ff_1 (.D(AMUX), .clk(CLOCK), .Q(Q18));  // open: Qn, preset, reset
  D_Flip_Flop d_ff_2 (.D(ULA), .clk(CLOCK), .Q(Q17));  // open: Qn, preset, reset
  D_Flip_Flop d_ff_3 (.D(ULA1), .clk(CLOCK), .Q(Q16));  // open: Qn, preset, reset
  D_Flip_Flop d_ff_4 (.D(SH), .clk(CLOCK), .Q(Q15));  // open: Qn, preset, reset
  D_Flip_Flop d_ff_5 (.D(SH1), .clk(CLOCK), .Q(Q14));  // open: Qn, preset, reset
  D_Flip_Flop d_ff_6 (.D(MAR), .clk(CLOCK), .Q(Q13));  // open: Qn, preset, reset
  D_Flip_Flop d_ff_7 (.D(MBR), .clk(CLOCK), .Q(Q12));  // open: Qn, preset, reset
  D_Flip_Flop d_ff_8 (.D(RD), .clk(CLOCK), .Q(Q11));  // open: Qn, preset, reset
  D_Flip_Flop d_ff_9 (.D(WR), .clk(CLOCK), .Q(Q10));  // open: Qn, preset, reset
  D_Flip_Flop d_ff_10 (.D(ENC), .clk(CLOCK), .Q(Q9));  // open: Qn, preset, reset
  D_Flip_Flop d_ff_11 (.D(DECC), .clk(CLOCK), .Q(Q8));  // open: Qn, preset, reset
  D_Flip_Flop d_ff_12 (.D(DECC1), .clk(CLOCK), .Q(Q7));  // open: Qn, preset, reset
  D_Flip_Flop d_ff_13 (.D(DECC2), .clk(CLOCK), .Q(Q6));  // open: Qn, preset, reset
  D_Flip_Flop d_ff_14 (.D(DECA), .clk(CLOCK), .Q(Q5));  // open: Qn, preset, reset
  D_Flip_Flop d_ff_15 (.D(DECA1), .clk(CLOCK), .Q(Q4));  // open: Qn, preset, reset
  D_Flip_Flop d_ff_16 (.D(DECA2), .clk(CLOCK), .Q(Q3));  // open: Qn, preset, reset
  D_Flip_Flop d_ff_17 (.D(DECB), .clk(CLOCK), .Q(Q2));  // open: Qn, preset, reset
  D_Flip_Flop d_ff_18 (.D(DECB1), .clk(CLOCK), .Q(Q1));  // open: Qn, preset, reset
  D_Flip_Flop d_ff_19 (.D(DECB2), .clk(CLOCK), .Q(Q0));  // open: Qn, preset, reset
endmodule

module PC (
  input  E5,
  input  E4,
  input  E3,
  input  E2,
  input  E1,
  input  E0,
  input  MUX,
  input  CLOCK,
  input  ENABLE,
  input  RESET,
  output Y5,
  output Y4,
  output Y3,
  output Y2,
  output Y1,
  output Y0
);

  wire resgitrador_1_p10, resgitrador_1_p11, resgitrador_1_p12, resgitrador_1_p13, somador_6bit_1_sum0,
       somador_6bit_1_sum1, somador_6bit_1_sum2, somador_6bit_1_sum3, somador_6bit_1_sum4,
       somador_6bit_1_sum5;

  // Resgitrador resgitrador_1: pin names not known; wires that end beside it: E0, E1, E2, E3, E4, E5, CLOCK, ENABLE, RESET, resgitrador_1_p10, resgitrador_1_p11, resgitrador_1_p12, resgitrador_1_p13, resgitrador_1_p10, resgitrador_1_p10
  Somador_6bit somador_6bit_1 (
    .A5(resgitrador_1_p10), .A4(resgitrador_1_p10), .A3(resgitrador_1_p13), .A2(resgitrador_1_p12),
    .A1(resgitrador_1_p11), .A0(resgitrador_1_p10), .B0(1'b1), .SUM5(somador_6bit_1_sum5),
    .SUM4(somador_6bit_1_sum4), .SUM3(somador_6bit_1_sum3), .SUM2(somador_6bit_1_sum2),
    .SUM1(somador_6bit_1_sum1), .SUM0(somador_6bit_1_sum0));  // open: B5, B4, B3, B2, B1, Cout
  Multiplexador_2x1 multiplexador_2x1_1 (.S1(somador_6bit_1_sum0), .S0(resgitrador_1_p10), .E0(MUX), .Y(Y0));
  Multiplexador_2x1 multiplexador_2x1_2 (.S1(somador_6bit_1_sum1), .S0(resgitrador_1_p11), .E0(MUX), .Y(Y1));
  Multiplexador_2x1 multiplexador_2x1_3 (.S1(somador_6bit_1_sum2), .S0(resgitrador_1_p12), .E0(MUX), .Y(Y2));
  Multiplexador_2x1 multiplexador_2x1_4 (.S1(somador_6bit_1_sum3), .S0(resgitrador_1_p13), .E0(MUX), .Y(Y3));
  Multiplexador_2x1 multiplexador_2x1_5 (.S1(somador_6bit_1_sum4), .S0(resgitrador_1_p10), .E0(MUX), .Y(Y4));
  Multiplexador_2x1 multiplexador_2x1_6 (.S1(somador_6bit_1_sum5), .S0(resgitrador_1_p10), .E0(MUX), .Y(Y5));
endmodule

module Teste (
  input  e,
  input  s,
  output se
);

  and and_1 (se, e, e);
  and and_2 (e, s, s);
endmodule

module TRANSCRIVER (
  input  TEC0,
  input  TEC1,
  input  TEC2,
  input  TEC3,
  input  TEC4,
  input  TEC5,
  input  BUSEXT0,
  input  BUSEXT1,
  input  BUSEXT2,
  input  BUSEXT3,
  input  BUSEXT4,
  input  BUSEXT5,
  input  T_R,
  output DIS0,
  output DIS1,
  output DIS2,
  output DIS3,
  output DIS4,
  output DIS5,
  output SEXT0,
  output SEXT1,
  output SEXT2,
  output SEXT3,
  output SEXT4,
  output SEXT5
);

  wire decode_1x2_1_s0, decode_1x2_1_s1;

  Decode_1x2 decode_1x2_1 (.E0(T_R), .S1(decode_1x2_1_s1), .S0(decode_1x2_1_s0));
  assign SEXT5 = decode_1x2_1_s0 ? TEC5 : 1'bz;  // Controlled_Buffer controlled_buffer_1
  assign SEXT4 = decode_1x2_1_s0 ? TEC4 : 1'bz;  // Controlled_Buffer controlled_buffer_2
  assign SEXT3 = decode_1x2_1_s0 ? TEC3 : 1'bz;  // Controlled_Buffer controlled_buffer_3
  assign SEXT2 = decode_1x2_1_s0 ? TEC2 : 1'bz;  // Controlled_Buffer controlled_buffer_4
  assign SEXT1 = decode_1x2_1_s0 ? TEC1 : 1'bz;  // Controlled_Buffer controlled_buffer_5
  assign SEXT0 = decode_1x2_1_s0 ? TEC0 : 1'bz;  // Controlled_Buffer controlled_buffer_6
  assign DIS5 = decode_1x2_1_s1 ? BUSEXT5 : 1'bz;  // Controlled_Buffer controlled_buffer_7
  assign DIS4 = decode_1x2_1_s1 ? BUSEXT4 : 1'bz;  // Controlled_Buffer controlled_buffer_8
  assign DIS3 = decode_1x2_1_s1 ? BUSEXT3 : 1'bz;  // Controlled_Buffer controlled_buffer_9
  assign DIS2 = decode_1x2_1_s1 ? BUSEXT2 : 1'bz;  // Controlled_Buffer controlled_buffer_10
  assign DIS1 = decode_1x2_1_s1 ? BUSEXT1 : 1'bz;  // Controlled_Buffer controlled_buffer_11
  assign DIS0 = decode_1x2_1_s1 ? BUSEXT0 : 1'bz;  // Controlled_Buffer controlled_buffer_12
endmodule

module PROCESSADOR_TESTES (
  input  RXTX,
  input  in_2,
  input  in_3,
  input  CP,
  input  ENABLE
);

  wire amux_1_a0, amux_1_a1, amux_1_a2, amux_1_a3, amux_1_a4, amux_1_a5, banco_registrador_1_a0,
       banco_registrador_1_a1, banco_registrador_1_a2, banco_registrador_1_a3, banco_registrador_1_a4,
       banco_registrador_1_a5, banco_registrador_1_b0, banco_registrador_1_b1, banco_registrador_1_b2,
       banco_registrador_1_b3, banco_registrador_1_b4, banco_registrador_1_b5, Controle,
       controlled_buffer_1_out, controlled_buffer_2_out, controlled_buffer_3_out, controlled_buffer_4_out,
       controlled_buffer_5_out, controlled_buffer_6_out, controlled_buffer_7_out, controlled_buffer_9_out,
       controlled_buffer_10_out, controlled_buffer_11_out, controlled_buffer_12_out,
       controlled_buffer_13_out, controlled_buffer_14_out, controlled_buffer_16_out,
       controlled_buffer_17_out, controlled_buffer_20_out, controlled_buffer_21_out,
       controlled_buffer_24_out, controlled_buffer_25_out, controlled_buffer_28_out,
       controlled_buffer_29_out, controlled_buffer_32_out, controlled_buffer_33_out,
       controlled_buffer_36_out, d_ff_1_q, d_ff_1_qn, d_ff_2_q, d_ff_2_qn, d_ff_3_q, d_ff_3_qn, d_ff_4_q,
       d_ff_4_qn, d_ff_5_q, d_ff_5_qn, d_ff_6_q, d_ff_6_qn, decode_1x2_1_s0, decode_1x2_1_s1,
       decode_2bits_1_s3, latch_a_1_s0, latch_a_1_s1, latch_a_1_s2, latch_a_1_s3, latch_a_1_s4, latch_a_1_s5,
       latch_b_1_s0, latch_b_1_s1, latch_b_1_s2, latch_b_1_s3, latch_b_1_s4, latch_b_1_s5, or_1_out,
       or_2_out, or_3_out, or_4_out, or_5_out, or_6_out, or_7_out, or_8_out, or_9_out, or_10_out, or_11_out,
       or_12_out, S0, S1, S2, shifter_projeto_1_s0, shifter_projeto_1_s1, shifter_projeto_1_s2,
       shifter_projeto_1_s3, shifter_projeto_1_s4, shifter_projeto_1_s5, ula_6bits_1_r0, ula_6bits_1_r1,
       ula_6bits_1_r2, ula_6bits_1_r3, ula_6bits_1_r4, ula_6bits_1_r5, undriven, undriven_2, undriven_3,
       undriven_4, undriven_5, undriven_6;

  and and_1 (Controle, CP, ENABLE);
  Decode_2bits decode_2bits_1 (.E1(in_3), .E0(in_2), .S3(decode_2bits_1_s3), .S2(S2), .S1(S1), .S0(S0));
  // NoConnect on decode_2bits_1_s3
  Decode_1x2 decode_1x2_1 (.E0(RXTX), .S1(decode_1x2_1_s1), .S0(decode_1x2_1_s0));
  assign controlled_buffer_1_out = decode_1x2_1_s0 ? undriven : 1'bz;  // Controlled_Buffer controlled_buffer_1
  assign controlled_buffer_2_out = decode_1x2_1_s0 ? undriven_2 : 1'bz;  // Controlled_Buffer controlled_buffer_2
  assign controlled_buffer_3_out = decode_1x2_1_s0 ? undriven_3 : 1'bz;  // Controlled_Buffer controlled_buffer_3
  assign controlled_buffer_4_out = decode_1x2_1_s0 ? undriven_4 : 1'bz;  // Controlled_Buffer controlled_buffer_4
  assign controlled_buffer_5_out = decode_1x2_1_s0 ? undriven_5 : 1'bz;  // Controlled_Buffer controlled_buffer_5
  assign controlled_buffer_6_out = decode_1x2_1_s0 ? undriven_6 : 1'bz;  // Controlled_Buffer controlled_buffer_6
  assign controlled_buffer_7_out = S2 ? controlled_buffer_1_out : 1'bz;  // Controlled_Buffer controlled_buffer_7
  D_Flip_Flop d_ff_1 (
    .D(controlled_buffer_7_out), .clk(Controle), .Q(d_ff_1_q), .Qn(d_ff_1_qn));  // open: preset, reset
  assign controlled_buffer_7_out = or_1_out ? shifter_projeto_1_s5 : 1'bz;  // Controlled_Buffer controlled_buffer_8
  or or_1 (or_1_out, S0, S1);
  assign controlled_buffer_9_out = decode_1x2_1_s1 ? controlled_buffer_1_out : 1'bz;  // Controlled_Buffer controlled_buffer_9
  assign controlled_buffer_10_out = decode_1x2_1_s1 ? controlled_buffer_2_out : 1'bz;  // Controlled_Buffer controlled_buffer_10
  assign controlled_buffer_11_out = decode_1x2_1_s1 ? controlled_buffer_3_out : 1'bz;  // Controlled_Buffer controlled_buffer_11
  assign controlled_buffer_12_out = decode_1x2_1_s1 ? controlled_buffer_4_out : 1'bz;  // Controlled_Buffer controlled_buffer_12
  assign controlled_buffer_13_out = decode_1x2_1_s1 ? controlled_buffer_5_out : 1'bz;  // Controlled_Buffer controlled_buffer_13
  assign controlled_buffer_14_out = decode_1x2_1_s1 ? controlled_buffer_6_out : 1'bz;  // Controlled_Buffer controlled_buffer_14
  assign controlled_buffer_1_out = S1 ? d_ff_1_q : 1'bz;  // Controlled_Buffer controlled_buffer_15
  or or_2 (or_2_out, S2, S0);
  // NoConnect on d_ff_1_qn
  assign controlled_buffer_16_out = or_2_out ? d_ff_1_q : 1'bz;  // Controlled_Buffer controlled_buffer_16
  or or_3 (or_3_out, S0, S1);
  or or_4 (or_4_out, S2, S0);
  assign controlled_buffer_17_out = S2 ? controlled_buffer_2_out : 1'bz;  // Controlled_Buffer controlled_buffer_17
  D_Flip_Flop d_ff_2 (
    .D(controlled_buffer_17_out), .clk(Controle), .Q(d_ff_2_q), .Qn(d_ff_2_qn));  // open: preset, reset
  assign controlled_buffer_17_out = or_3_out ? shifter_projeto_1_s4 : 1'bz;  // Controlled_Buffer controlled_buffer_18
  assign controlled_buffer_2_out = S1 ? d_ff_2_q : 1'bz;  // Controlled_Buffer controlled_buffer_19
  // NoConnect on d_ff_2_qn
  assign controlled_buffer_20_out = or_4_out ? d_ff_2_q : 1'bz;  // Controlled_Buffer controlled_buffer_20
  assign controlled_buffer_21_out = S2 ? controlled_buffer_3_out : 1'bz;  // Controlled_Buffer controlled_buffer_21
  D_Flip_Flop d_ff_3 (
    .D(controlled_buffer_21_out), .clk(Controle), .Q(d_ff_3_q), .Qn(d_ff_3_qn));  // open: preset, reset
  assign controlled_buffer_21_out = or_5_out ? shifter_projeto_1_s3 : 1'bz;  // Controlled_Buffer controlled_buffer_22
  or or_5 (or_5_out, S0, S1);
  assign controlled_buffer_3_out = S1 ? d_ff_3_q : 1'bz;  // Controlled_Buffer controlled_buffer_23
  or or_6 (or_6_out, S2, S0);
  // NoConnect on d_ff_3_qn
  assign controlled_buffer_24_out = or_6_out ? d_ff_3_q : 1'bz;  // Controlled_Buffer controlled_buffer_24
  or or_7 (or_7_out, S0, S1);
  or or_8 (or_8_out, S2, S0);
  assign controlled_buffer_25_out = S2 ? controlled_buffer_4_out : 1'bz;  // Controlled_Buffer controlled_buffer_25
  D_Flip_Flop d_ff_4 (
    .D(controlled_buffer_25_out), .clk(Controle), .Q(d_ff_4_q), .Qn(d_ff_4_qn));  // open: preset, reset
  assign controlled_buffer_25_out = or_7_out ? shifter_projeto_1_s2 : 1'bz;  // Controlled_Buffer controlled_buffer_26
  assign controlled_buffer_4_out = S1 ? d_ff_4_q : 1'bz;  // Controlled_Buffer controlled_buffer_27
  // NoConnect on d_ff_4_qn
  assign controlled_buffer_28_out = or_8_out ? d_ff_4_q : 1'bz;  // Controlled_Buffer controlled_buffer_28
  assign controlled_buffer_29_out = S2 ? controlled_buffer_5_out : 1'bz;  // Controlled_Buffer controlled_buffer_29
  D_Flip_Flop d_ff_5 (
    .D(controlled_buffer_29_out), .clk(Controle), .Q(d_ff_5_q), .Qn(d_ff_5_qn));  // open: preset, reset
  assign controlled_buffer_29_out = or_9_out ? shifter_projeto_1_s1 : 1'bz;  // Controlled_Buffer controlled_buffer_30
  or or_9 (or_9_out, S0, S1);
  assign controlled_buffer_5_out = S1 ? d_ff_5_q : 1'bz;  // Controlled_Buffer controlled_buffer_31
  or or_10 (or_10_out, S2, S0);
  // NoConnect on d_ff_5_qn
  assign controlled_buffer_32_out = or_10_out ? d_ff_5_q : 1'bz;  // Controlled_Buffer controlled_buffer_32
  or or_11 (or_11_out, S0, S1);
  or or_12 (or_12_out, S2, S0);
  assign controlled_buffer_33_out = S2 ? controlled_buffer_6_out : 1'bz;  // Controlled_Buffer controlled_buffer_33
  D_Flip_Flop d_ff_6 (
    .D(controlled_buffer_33_out), .clk(Controle), .Q(d_ff_6_q), .Qn(d_ff_6_qn));  // open: preset, reset
  assign controlled_buffer_33_out = or_11_out ? shifter_projeto_1_s0 : 1'bz;  // Controlled_Buffer controlled_buffer_34
  MAR mar_1 (
    .B5(latch_b_1_s5), .B4(latch_b_1_s4), .B3(latch_b_1_s3), .B2(latch_b_1_s2), .B1(latch_b_1_s1),
    .B0(latch_b_1_s0));  // open: CLOCK, ENABLE, RESET, S5, S4, S3, S2, S1, S0
  assign controlled_buffer_6_out = S1 ? d_ff_6_q : 1'bz;  // Controlled_Buffer controlled_buffer_35
  // NoConnect on d_ff_6_qn
  assign controlled_buffer_36_out = or_12_out ? d_ff_6_q : 1'bz;  // Controlled_Buffer controlled_buffer_36
  Banco_Registrador banco_registrador_1 (
    .E5(shifter_projeto_1_s5), .E4(shifter_projeto_1_s4), .E3(shifter_projeto_1_s3),
    .E2(shifter_projeto_1_s2), .E1(shifter_projeto_1_s1), .E0(shifter_projeto_1_s0),
    .A5(banco_registrador_1_a5), .A4(banco_registrador_1_a4), .A3(banco_registrador_1_a3),
    .A2(banco_registrador_1_a2), .A1(banco_registrador_1_a1), .A0(banco_registrador_1_a0),
    .B5(banco_registrador_1_b5), .B4(banco_registrador_1_b4), .B3(banco_registrador_1_b3),
    .B2(banco_registrador_1_b2), .B1(banco_registrador_1_b1), .B0(banco_registrador_1_b0));  // open: AA2, AA1, AA0, BB2, BB1, BB0, C2, C1, C0, in_10, ENABLE
  Amux amux_1 (
    .M5(latch_a_1_s5), .M4(latch_a_1_s4), .M3(latch_a_1_s3), .M2(latch_a_1_s2), .M1(latch_a_1_s1),
    .M0(latch_a_1_s0), .L5(controlled_buffer_16_out), .L4(controlled_buffer_20_out),
    .L3(controlled_buffer_24_out), .L2(controlled_buffer_28_out), .L1(controlled_buffer_32_out),
    .L0(controlled_buffer_36_out), .A5(amux_1_a5), .A4(amux_1_a4), .A3(amux_1_a3), .A2(amux_1_a2),
    .A1(amux_1_a1), .A0(amux_1_a0));  // open: E0
  Shifter_projeto shifter_projeto_1 (
    .R5(ula_6bits_1_r5), .R4(ula_6bits_1_r4), .R3(ula_6bits_1_r3), .R2(ula_6bits_1_r2), .R1(ula_6bits_1_r1),
    .R0(ula_6bits_1_r0), .S5(shifter_projeto_1_s5), .S4(shifter_projeto_1_s4), .S3(shifter_projeto_1_s3),
    .S2(shifter_projeto_1_s2), .S1(shifter_projeto_1_s1), .S0(shifter_projeto_1_s0));  // open: Ee1, Ee0
  LATCH_A latch_a_1 (
    .A5(banco_registrador_1_a5), .A4(banco_registrador_1_a4), .A3(banco_registrador_1_a3),
    .A2(banco_registrador_1_a2), .A1(banco_registrador_1_a1), .A0(banco_registrador_1_a0), .S5(latch_a_1_s5),
    .S4(latch_a_1_s4), .S3(latch_a_1_s3), .S2(latch_a_1_s2), .S1(latch_a_1_s1), .S0(latch_a_1_s0));  // open: ENABLE
  ULA_6bits ula_6bits_1 (
    .A4(amux_1_a4), .A3(amux_1_a3), .A2(amux_1_a2), .A1(amux_1_a1), .A0(amux_1_a0), .B5(latch_b_1_s5),
    .B4(latch_b_1_s4), .B3(latch_b_1_s3), .B2(latch_b_1_s2), .B1(latch_b_1_s1), .B0(latch_b_1_s0),
    .A5(amux_1_a5), .R5(ula_6bits_1_r5), .R4(ula_6bits_1_r4), .R3(ula_6bits_1_r3), .R2(ula_6bits_1_r2),
    .R1(ula_6bits_1_r1), .R0(ula_6bits_1_r0));  // open: E1, E0
  LATCH_B latch_b_1 (
    .B5(banco_registrador_1_b5), .B4(banco_registrador_1_b4), .B3(banco_registrador_1_b3),
    .B2(banco_registrador_1_b2), .B1(banco_registrador_1_b1), .B0(banco_registrador_1_b0), .S5(latch_b_1_s5),
    .S4(latch_b_1_s4), .S3(latch_b_1_s3), .S2(latch_b_1_s2), .S1(latch_b_1_s1), .S0(latch_b_1_s0));  // open: ENABLE

  // Notes on the sheet:
  //   CONTROLE
  //   TEMPO
  //   Transcriber
  //   Display
  //   Keyboard
endmodule

module Banco_Mir (
  input  in_1,
  input  in_2,
  input  in_3,
  input  in_4,
  input  in_5,
  output Q0,
  output Q1,
  output Q2,
  output Q3,
  output Q4,
  output Q5,
  output Q6,
  output Q7,
  output Q8,
  output Q9,
  output Q10,
  output Q11,
  output Q12,
  output Q13,
  output Q14,
  output Q15,
  output Q16,
  output Q17,
  output Q18,
  output Q19,
  output Q20,
  output Q21,
  output Q22,
  output Q23
);

  ROM #(.addrWidth(5), .dataWidth(24)) rom_1 (
    .addr({in_1, in_2, in_3, in_4, in_5}),
    .data({Q23, Q22, Q21, Q20, Q19, Q18, Q17, Q16, Q15, Q14, Q13, Q12, Q11, Q10, Q9, Q8, Q7, Q6, Q5, Q4, Q3, Q2, Q1, Q0}));

  // Notes on the sheet:
  //   contents of rom_1 (hex, n*v repeats v):
  //   201 20200 20201 30201 14200 18200 10208 10210 10218 10220 10228 10230 10238 10240 10280 102c0 10300
  //   10340 10380 103c0 12000 50200 11800 11400 11800
endmodule

module Programa (
  input  E0,
  input  E1,
  input  E2,
  input  E3,
  input  E4,
  output S0,
  output S1,
  output S2,
  output S3,
  output S4
);

  ROM #(.addrWidth(5), .dataWidth(5)) rom_1 (.addr({E4, E3, E2, E1, E0}), .data({S4, S3, S2, S1, S0}));

  // Notes on the sheet:
  //   contents of rom_1 (hex, n*v repeats v):
  //   d 3 13 1 4 1 12 1 5 1 d 4 14 17 15 4 0 e b 14 7 16 18
endmodule

module Incrementador (
  input  DADOS,
  input  CLEAR,
  output S0,
  output S1,
  output S2,
  output S3,
  output S4
);

  Counter #(.max('h1f), .width(5)) counter_1 (
    .Q({S4, S3, S2, S1, S0}), .clk(DADOS), .clr(CLEAR));  // open: load, D, count, carry, up
  Hex_Digit_Display #(.decimalPoint("false")) A (.value({3'b000, S4}));
  Hex_Digit_Display #(.decimalPoint("false")) B (.value({S3, S2, S1, S0}));
endmodule

module aaaa (
);

  Programa programa_1 ();  // open: E0, E1, E2, E3, E4, S0, S1, S2, S3, S4
endmodule
